// Logisim project control-logic.circ as structural Verilog: 1 circuit, main circuit control_logic
module control_logic (
  input  [31:0] inst,
  input  BrEq,
  input  BrLt,
  output PCSel,
  output RegWEn,
  output [2:0] ImmSel,
  output BrUn,
  output ASel,
  output BSel,
  output [3:0] ALUSel,
  output MemRW,
  output [1:0] WBSel,
  output CSRSel,
  output CSRWen
);

  wire comparator_2_eq, comparator_3_eq, comparator_6_eq, comparator_7_eq, I_f, R_f, S_f, SB_f, U_f, UJ_f;
  wire [6:0] opcode;

  BitSelector #(.group(7), .width(32)) bitselector_1 (.in(inst), .out(opcode), .sel(3'b000));
  Comparator #(.mode("unsigned"), .width(7)) comparator_1 (.a(opcode), .b(7'b0110011), .eq(R_f));  // open: gt, lt
  Comparator #(.mode("unsigned"), .width(7)) comparator_2 (
    .a(opcode), .b(7'b0000011), .eq(comparator_2_eq));  // open: gt, lt
  Comparator #(.mode("unsigned"), .width(7)) comparator_3 (
    .a(opcode), .b(7'b0010011), .eq(comparator_3_eq));  // open: gt, lt
  Comparator #(.mode("unsigned"), .width(7)) comparator_4 (.a(opcode), .b(7'b0100011), .eq(S_f));  // open: gt, lt
  Comparator #(.mode("unsigned"), .width(7)) comparator_5 (.a(opcode), .b(7'b1100011), .eq(SB_f));  // open: gt, lt
  Comparator #(.mode("unsigned"), .width(7)) comparator_6 (
    .a(opcode), .b(7'b0010111), .eq(comparator_6_eq));  // open: gt, lt
  Comparator #(.mode("unsigned"), .width(7)) comparator_7 (
    .a(opcode), .b(7'b0110111), .eq(comparator_7_eq));  // open: gt, lt
  Comparator #(.mode("unsigned"), .width(7)) comparator_8 (.a(opcode), .b(7'b1101111), .eq(UJ_f));  // open: gt, lt
  or or_1 (I_f, comparator_2_eq, comparator_3_eq);
  or or_2 (U_f, comparator_6_eq, comparator_7_eq);

  assign ALUSel = 4'b0000;
  assign ASel = 1'b0;
  assign BSel = 1'b1;
  assign PCSel = 1'b0;
  assign RegWEn = 1'b1;
  assign WBSel = 2'b01;

  // Notes on the sheet:
  //   INPUTS to your circuit
  //   DON'T CHANGE THE LOCATIONS OF THE INPUTS AND OUTPUTS!
  //   OUTPUT from your circuit
endmodule
